// Logisim project proyectoFinal.circ as structural Verilog: 1 circuit, main circuit main
module main (
);

  wire button_1_out, d_ff_1_q, d_ff_2_q, dipswitch_1_sw5, dipswitch_1_sw6, dipswitch_1_sw7, dipswitch_1_sw8,
       dipswitch_2_sw5, dipswitch_2_sw6, dipswitch_2_sw7, dipswitch_2_sw8, n7404_1_pin2, n7404_1_pin3,
       n7404_1_pin4, n7404_1_pin12, n7408_1_pin1, n7408_1_pin2, n7408_1_pin3, n7408_1_pin5, n7408_1_pin6,
       n7408_1_pin8, n7408_1_pin9, n7408_1_pin11, n7408_1_pin12, n7408_2_pin4, n7408_2_pin5, n7408_2_pin6,
       n7408_2_pin10, n7408_2_pin11, n7408_2_pin12, n7408_3_pin1, n7408_3_pin3, n7408_3_pin5, n7408_3_pin8,
       n747266_1_pin1, n747266_1_pin2, n747266_1_pin4, n747266_1_pin5, n747266_1_pin9, n747266_1_pin10,
       n747266_1_pin12, n747266_1_pin13;

  _7408 u_7408_1 (
    .pin1(n7408_1_pin1), .pin2(n7408_1_pin2), .pin3(n7408_1_pin3), .pin4(n7408_1_pin3), .pin5(n7408_1_pin5),
    .pin6(n7408_1_pin6), .pin13(n7408_1_pin6), .pin12(n7408_1_pin12), .pin11(n7408_1_pin11),
    .pin10(n7408_1_pin11), .pin9(n7408_1_pin9), .pin8(n7408_1_pin8));
  _747266 u_747266_1 (
    .pin1(n747266_1_pin1), .pin2(n747266_1_pin2), .pin3(n7408_1_pin1), .pin4(n747266_1_pin4),
    .pin5(n747266_1_pin5), .pin6(n7408_1_pin12), .pin13(n747266_1_pin13), .pin12(n747266_1_pin12),
    .pin11(n7408_1_pin2), .pin10(n747266_1_pin10), .pin9(n747266_1_pin9), .pin8(n7408_1_pin5));
  DipSwitch dipswitch_1 (
    .sw1(n747266_1_pin1), .sw2(n747266_1_pin4), .sw3(n747266_1_pin13), .sw4(n747266_1_pin10),
    .sw5(dipswitch_1_sw5), .sw6(dipswitch_1_sw6), .sw7(dipswitch_1_sw7), .sw8(dipswitch_1_sw8));
  DipSwitch dipswitch_2 (
    .sw1(n747266_1_pin2), .sw2(n747266_1_pin5), .sw3(n747266_1_pin12), .sw4(n747266_1_pin9),
    .sw5(dipswitch_2_sw5), .sw6(dipswitch_2_sw6), .sw7(dipswitch_2_sw7), .sw8(dipswitch_2_sw8));
  _7408 u_7408_2 (
    .pin4(n7408_2_pin4), .pin5(n7408_2_pin5), .pin6(n7408_2_pin6), .pin13(n7408_1_pin8),
    .pin12(n7408_2_pin12), .pin11(n7408_2_pin11), .pin10(n7408_2_pin10), .pin9(n7408_2_pin11),
    .pin8(n7408_2_pin4));  // open: pin1, pin2, pin3
  _747266 u_747266_2 (
    .pin1(dipswitch_1_sw5), .pin2(dipswitch_2_sw5), .pin3(n7408_1_pin9), .pin4(dipswitch_1_sw6),
    .pin5(dipswitch_2_sw6), .pin6(n7408_2_pin5), .pin13(dipswitch_1_sw7), .pin12(dipswitch_2_sw7),
    .pin11(n7408_2_pin10), .pin10(dipswitch_1_sw8), .pin9(dipswitch_2_sw8), .pin8(n7408_2_pin12));
  LED led_1 (.in(n7408_3_pin3));
  LED led_2 (.in(n7408_3_pin5));
  D_Flip_Flop d_ff_1 (.D(n7408_3_pin5), .clk(button_1_out), .Q(d_ff_1_q), .reset(n7408_3_pin8));  // open: Qn, preset
  Button button_1 (.out(button_1_out));
  _7404 u_7404_1 (
    .pin1(d_ff_1_q), .pin2(n7404_1_pin2), .pin3(n7404_1_pin3), .pin4(n7404_1_pin4), .pin13(n7408_2_pin6),
    .pin12(n7404_1_pin12));  // open: pin5, pin6, pin11, pin10, pin9, pin8
  D_Flip_Flop d_ff_2 (.D(n7408_3_pin3), .clk(button_1_out), .Q(d_ff_2_q), .reset(n7408_3_pin8));  // open: Qn, preset
  _7408 u_7408_3 (
    .pin1(n7408_3_pin1), .pin2(n7404_1_pin12), .pin3(n7408_3_pin3), .pin4(n7408_3_pin3), .pin5(n7408_3_pin5),
    .pin6(n7404_1_pin3), .pin13(n7404_1_pin12), .pin12(n7404_1_pin2), .pin11(n7408_3_pin5),
    .pin10(n7404_1_pin4), .pin9(n7408_2_pin6), .pin8(n7408_3_pin8));
  _7486 u_7486_1 (
    .pin13(d_ff_1_q), .pin12(d_ff_2_q), .pin11(n7408_3_pin1));  // open: pin1, pin2, pin3, pin4, pin5, pin6, pin10, pin9, pin8

  // Notes on the sheet:
  //   LOCK_REAL
  //   LOCK
endmodule
